# Fritzing sketch Weather Station (saved by Fritzing 0.9.2b)
breadboards: 1

parts:
  Raspberry_Pi1 = Raspberry Pi B+
  U1 = BMP085 Pressure Sensor [package=bmp085]
  DHT2 = DHT22 Humidity and Temperature Sensor
  GY-NEO6MV3 = SUP500F [package=sup500f]
  R1 = Resistor [tolerance=±20% resistance=10k package=THT]

nets:
  3V3: Raspberry_Pi1.3v3, U1.VDDD, DHT2.VDD, GY-NEO6MV3.VCC, R1.Pin_0
  N1: Raspberry_Pi1.GPIO2, U1.SDA
  N2: Raspberry_Pi1.GPIO3, U1.SCL
  N3: Raspberry_Pi1.GPIO4, DHT2.DATA, R1.Pin_1
  GND: Raspberry_Pi1.GND, U1.GND, DHT2.GND, GY-NEO6MV3.GND
  N4: Raspberry_Pi1.GPIO15, GY-NEO6MV3.TX-O
  N5: Raspberry_Pi1.GPIO14, GY-NEO6MV3.RX-I
